// Logisim project ProyectoMIPS.circ as structural Verilog: 4 circuits, main circuit main
// address
module main (
  input  in_1,
  input  Active_Store,
  input  Active_Load,
  input  [31:0] in_4,
  output [31:0] out_5
);

  wire clock;
  wire [23:0] pc_1_address;

  Clock clock_1 (.out(clock));
  PC pc_1 (.Reset(in_1), .Clock(clock), .Address(pc_1_address));
  RAM #(.addrWidth(24), .dataWidth(32), .bus("separate")) ram_1 (
    .addr(pc_1_address), .din(in_4), .data(out_5), .str(Active_Store), .clk(clock), .ld(Active_Load));  // open: sel, clr

  // Notes on the sheet:
  //   FETCH
endmodule

module PC (
  input  Clock,
  input  Reset,
  output [23:0] Address
);

  wire [23:0] adder_1_out;

  Adder #(.width(24)) adder_1 (.a(Address), .b(24'h1), .out(adder_1_out));  // open: cin, cout
  Register #(.width(24)) register_1 (.D(adder_1_out), .Q(Address), .clk(Clock), .clr(Reset));  // open: en
endmodule

module Show (
);

  Multiplexer multiplexer_1 ();  // open: in0, in1, out, sel, en
endmodule

module Show_Will (
  input  [7:0] in_1,
  input  [7:0] in_2,
  input  [7:0] in_3,
  input  [4:0] rs,
  input  [4:0] rt,
  input  [7:0] in_6,
  input  [7:0] in_7,
  input  [7:0] in_8,
  input  [4:0] rd,
  input  [4:0] shamt,
  input  [5:0] Funct,
  input  [7:0] in_12,
  input  [7:0] in_13,
  input  [5:0] Op,
  output [7:0] out_15,
  output [7:0] out_16,
  output [7:0] out_17
);

  Hex_Digit_Display hex_digit_display_1 ();  // open: value, dp
  _7_Segment_Display u_7_segment_display_1 (
    .g(in_1[3]), .f(in_1[2]), .a(in_1[1]), .b(in_1[0]), .e(in_1[7]), .d(in_1[6]), .c(in_1[5]), .dp(in_1[4]));
  _7_Segment_Display u_7_segment_display_2 (
    .g(in_8[3]), .f(in_8[2]), .a(in_8[1]), .b(in_8[0]), .e(in_8[7]), .d(in_8[6]), .c(in_8[5]), .dp(in_8[4]));
  _7_Segment_Display u_7_segment_display_3 (
    .g(in_13[3]), .f(in_13[2]), .a(in_13[1]), .b(in_13[0]), .e(in_13[7]), .d(in_13[6]), .c(in_13[5]),
    .dp(in_13[4]));
  Multiplexer multiplexer_1 ();  // open: in0, in1, out, sel, en
  _7_Segment_Display u_7_segment_display_4 (
    .g(in_2[3]), .f(in_2[2]), .a(in_2[1]), .b(in_2[0]), .e(in_2[7]), .d(in_2[6]), .c(in_2[5]), .dp(in_2[4]));
  _7_Segment_Display u_7_segment_display_5 (
    .g(in_6[3]), .f(in_6[2]), .a(in_6[1]), .b(in_6[0]), .e(in_6[7]), .d(in_6[6]), .c(in_6[5]), .dp(in_6[4]));
  _7_Segment_Display u_7_segment_display_6 (
    .g(in_12[3]), .f(in_12[2]), .a(in_12[1]), .b(in_12[0]), .e(in_12[7]), .d(in_12[6]), .c(in_12[5]),
    .dp(in_12[4]));
  _7_Segment_Display u_7_segment_display_7 (
    .g(in_3[3]), .f(in_3[2]), .a(in_3[1]), .b(in_3[0]), .e(in_3[7]), .d(in_3[6]), .c(in_3[5]), .dp(in_3[4]));
  _7_Segment_Display u_7_segment_display_8 (
    .g(in_7[3]), .f(in_7[2]), .a(in_7[1]), .b(in_7[0]), .e(in_7[7]), .d(in_7[6]), .c(in_7[5]), .dp(in_7[4]));
endmodule
